# Fritzing sketch circuit (saved by Fritzing 0.9.3b)
breadboards: 2

parts:
  U1 = ESP32-38PinWide [part_number=ESP32-38PinWide]
  IC1 = 2.8 inch LCD SPI display with touch screen & SD card
  DFPlayer_Mini1 = DFPlayer MINI [package="DIP (Dual Inline) [THT]"]
  SP1 = SPEAKER [package=pcb_mount_speaker]

nets:
  N1: U1.3.3, DFPlayer_Mini1.VCC
  N2: U1.GND, IC1.pin2
  N3: U1.VIN, IC1.pin1
  N4: U1.GPIO16, DFPlayer_Mini1.TX
  N5: U1.GPIO17, DFPlayer_Mini1.RX
  N6: DFPlayer_Mini1.SPK1, SP1.+
  N7: DFPlayer_Mini1.SPK2, SP1.-

custom parts:
  ESP32-38PinWide: Generic 38-Pin ESP32 with wide format (only access to one side of pins on a breadboard) based on Stephen Lilley's HiLetgo ESP-WROOM-32 ESP32 ESP-32S Development Board.
  2.8 inch LCD SPI display with touch screen & SD card: A generic 2.8 inch LCD TFT 320x280 display with touchscreen and SD card slot.
  DFPlayer MINI: MP3 module by DFRobot.com for playing Music from an SD-Card. Supports WAV and MP3 files.
